# Fritzing sketch PhotogrammetryTurntable (saved by Fritzing 0.6.3b)
breadboards: 1

parts:
  Part1 = EasyDriver_v44
  Arduino1 = Arduino
  Power_plug1 = Power plug
  M1 = Stepper Motor - Bipolar
  S2 = Pushbutton [package="[SMD]"]
  R1 = Resistor [tolerance=±5% resistance=1.5k package="1206 [SMD]"]

nets:
  GND: Part1.GND, Arduino1.GND, Power_plug1.GND, R1.Pin_1
  N1: Part1.V+, Power_plug1.VCC
  N2: Part1.STEP, Arduino1.D5
  N3: Part1.DIR, Arduino1.D4
  N4: Part1.OUT2A, M1.A
  N5: Part1.OUT2B, M1.C
  N6: Part1.OUT1A, M1.B
  N7: Part1.OUT1B, M1.D
  VCC: Part1.VCC, Arduino1.+5V, S2.Pin_3, S2.Pin_4
  N8: Part1.SLEEP, Arduino1.D6
  N9: Arduino1.D3, S2.Pin_1, S2.Pin_2, R1.Pin_0
